// Logisim project TinyCPU-Peripherals.circ as structural Verilog: 4 circuits, main circuit TinyCPUSystemMain
module TinyCPUSystemMain (
  input  CLK,
  input  RESET,
  input  INTERRUPT_REQUEST,
  output [15:0] OUTPUT_PORT_VALUE,
  output OUTPUT_PORT_VALID,
  output INTERRUPT_ENABLED,
  output INTERRUPT_PENDING,
  output IN_INTERRUPT_HANDLER,
  output [11:0] RETURN_ADDRESS,
  output RETURN_ADDRESS_VALID
);
endmodule

module OutputPort (
  input  [15:0] WRITE_VALUE,
  input  WRITE_VALID,
  input  WRITE_ENABLE,
  input  CLK,
  input  RESET,
  output [15:0] VALUE,
  output VALID
);

  Register #(.width(16)) OUTPUT_VALUE (.D(WRITE_VALUE), .en(WRITE_ENABLE), .clk(CLK), .Q(VALUE), .clr(RESET));
  Register #(.width(1)) OUTPUT_VALID (.D(WRITE_VALID), .en(WRITE_ENABLE), .clk(CLK), .Q(VALID), .clr(RESET));

  // Notes on the sheet:
  //   AP-18 output port: value and validity are written atomically; reset clears both registers
endmodule

module OutputMemoryPath (
  input  [11:0] ADDRESS,
  input  [15:0] WRITE_VALUE,
  input  WRITE_VALID,
  input  WRITE_ENABLE,
  input  [15:0] RAM_READ_VALUE,
  input  RAM_READ_VALID,
  input  CLK,
  input  RESET,
  output [15:0] READ_VALUE,
  output READ_VALID,
  output RAM_WRITE_ENABLE,
  output [15:0] OUTPUT_PORT_VALUE,
  output OUTPUT_PORT_VALID
);

  wire NOT_OUTPUT_ADDRESS_out, RAM_WRITE_GATE_p2, RAM_WRITE_GATE_p4, RAM_WRITE_GATE_p6, undriven_2;
  wire [11:0] undriven;

  Comparator #(.width(12)) OUTPUT_ADDRESS_DECODE (.a(undriven), .b(ADDRESS));  // open: gt, eq, lt
  not NOT_OUTPUT_ADDRESS (NOT_OUTPUT_ADDRESS_out, undriven_2);
  // AND_Gate RAM_WRITE_GATE: pin names not known; wires that end beside it: WRITE_ENABLE, RAM_WRITE_GATE_p2, NOT_OUTPUT_ADDRESS_out, RAM_WRITE_GATE_p4, RAM_WRITE_GATE_p4, RAM_WRITE_GATE_p6, RAM_WRITE_ENABLE
  buf OUTPUT_WRITE_GATE (OUTPUT_PORT_VALID, RAM_WRITE_GATE_p2);  // AND_Gate
  Multiplexer #(.width(16)) OUTPUT_READ_VALUE_SELECT (
    .in0(RAM_READ_VALUE), .in1({OUTPUT_PORT_VALUE[15:1], WRITE_VALID}), .out(READ_VALUE));  // open: sel
  Multiplexer OUTPUT_READ_VALID_SELECT (.in0(RAM_READ_VALID), .in1(OUTPUT_PORT_VALID), .out(READ_VALID));  // open: sel
  // OutputPort OUTPUT_PORT: pin names not known; wires that end beside it: WRITE_VALUE, CLK, RESET
  // Pins of 1 and 16 bits meet at {OUTPUT_PORT_VALUE[15:1], WRITE_VALID}

  assign OUTPUT_PORT_VALUE[0] = WRITE_VALID;

  // Notes on the sheet:
  //   AP-18 address 0xfff bypasses RAM writes and selects the clocked output port for reads
endmodule

module InterruptController (
  input  INTERRUPT_REQUEST,
  input  INSTRUCTION_BOUNDARY,
  input  ENABLE_REQUEST,
  input  DISABLE_REQUEST,
  input  RETURN_REQUEST,
  input  [11:0] NEXT_PC,
  input  CLK,
  input  RESET,
  output INTERRUPT_ACCEPT,
  output [11:0] TARGET_PC,
  output INTERRUPT_ENABLED,
  output INTERRUPT_PENDING,
  output IN_INTERRUPT_HANDLER,
  output [11:0] RETURN_ADDRESS,
  output RETURN_ADDRESS_VALID,
  output ILLEGAL_RETURN
);

  wire INTERRUPT_ACCEPT_GATE_p3, INTERRUPT_ENABLED_p1, INTERRUPT_PENDING_p3, MASK_CLEAR_NOT_out,
       MASK_CLEAR_REQUEST_p4, MASK_HOLD_p3, MASK_SET_REQUEST_out, NOT_IN_HANDLER_out,
       PENDING_HOLD_UNTIL_ACCEPT_p4, PENDING_HOLD_UNTIL_ACCEPT_p5, PENDING_SET_OR_HOLD_out,
       PREVIOUS_REQUEST_NOT_out, REQUEST_LEVEL_q, RISING_EDGE_DETECT_out;
  wire [11:1] MASK_CLEAR_REQUEST_p3, RETURN_ADDRESS_q;

  or PENDING_SET_OR_HOLD (PENDING_SET_OR_HOLD_out, DISABLE_REQUEST, RETURN_REQUEST);
  // OR_Gate MASK_SET_REQUEST has open pins: out=MASK_SET_REQUEST_out
  // OR_Gate MASK_CLEAR_REQUEST: pin names not known; wires that end beside it: RETURN_REQUEST, DISABLE_REQUEST, {MASK_CLEAR_REQUEST_p3, INTERRUPT_ACCEPT}, MASK_CLEAR_REQUEST_p4
  Register #(.width(1)) REQUEST_LEVEL (.D(INTERRUPT_REQUEST), .en(1'b1), .clk(CLK), .Q(REQUEST_LEVEL_q), .clr(RESET));
  // Register #(.width(1)) INTERRUPT_ENABLED: pin names not known; wires that end beside it: INTERRUPT_ENABLED_p1, 1'b1, CLK, RESET
  // Register #(.width(1)) INTERRUPT_PENDING: pin names not known; wires that end beside it: PENDING_SET_OR_HOLD_out, 1'b1, INTERRUPT_PENDING_p3, RESET, INTERRUPT_PENDING
  Register #(.width(1)) u_IN_INTERRUPT_HANDLER (
    .D(NEXT_PC[0]), .en(INTERRUPT_ACCEPT), .clk(CLK), .Q(RETURN_ADDRESS[0]), .clr(RESET));
  Register #(.width(12)) u_RETURN_ADDRESS (
    .D({MASK_CLEAR_REQUEST_p3, INTERRUPT_ACCEPT}), .en(INTERRUPT_ACCEPT), .clk(CLK),
    .Q({RETURN_ADDRESS_q, RETURN_ADDRESS_VALID}), .clr(RESET));
  // Register #(.width(1)) RETURN_ADDRESS_VALID: pin names not known
  // NOT_Gate MASK_CLEAR_NOT has open pins: in=open, out=MASK_CLEAR_NOT_out
  not PREVIOUS_REQUEST_NOT (PREVIOUS_REQUEST_NOT_out, REQUEST_LEVEL_q);
  not NOT_IN_HANDLER (NOT_IN_HANDLER_out, RETURN_ADDRESS[0]);
  // AND_Gate MASK_HOLD: pin names not known; wires that end beside it: RESET, MASK_CLEAR_NOT_out, MASK_HOLD_p3, MASK_SET_REQUEST_out
  buf RISING_EDGE_DETECT (RISING_EDGE_DETECT_out, PREVIOUS_REQUEST_NOT_out);  // AND_Gate
  // AND_Gate INTERRUPT_ACCEPT_GATE: pin names not known; wires that end beside it: RESET, INSTRUCTION_BOUNDARY, INTERRUPT_ACCEPT_GATE_p3, NOT_IN_HANDLER_out, {MASK_CLEAR_REQUEST_p3, INTERRUPT_ACCEPT}
  // AND_Gate ILLEGAL_RETURN_GATE is placed but not wired
  // AND_Gate PENDING_HOLD_UNTIL_ACCEPT: pin names not known; wires that end beside it: INTERRUPT_PENDING, NOT_IN_HANDLER_out, INTERRUPT_ACCEPT_GATE_p3, PENDING_HOLD_UNTIL_ACCEPT_p4, PENDING_HOLD_UNTIL_ACCEPT_p5
  // OR_Gate MASK_NEXT has open pins: out=INTERRUPT_ENABLED_p1
  not INTERRUPT_ACCEPT_NOT (PENDING_HOLD_UNTIL_ACCEPT_p4, INTERRUPT_ACCEPT);
  // Multiplexer #(.width(12)) INTERRUPT_TARGET_SELECT: pin names not known
  // Pins of 1 and 12 bits meet at NEXT_PC
  // Pins of 1 and 12 bits meet at {MASK_CLEAR_REQUEST_p3, INTERRUPT_ACCEPT}
  // Pins of 1 and 12 bits meet at RETURN_ADDRESS
  // Pins of 1 and 12 bits meet at {RETURN_ADDRESS_q, RETURN_ADDRESS_VALID}

  assign INTERRUPT_ENABLED = RESET;

  // Notes on the sheet:
  //   AP-18 interrupt state: reset > accept at instruction boundary > instruction; rising edges remain pending while masked
endmodule
