// Logisim project TinyCPU_Peripherals.circ as structural Verilog: 5 circuits, main circuit TinyCPUSystemMain
module TinyCPUSystemMain (
  input  CLK,
  input  RESET,
  input  INTERRUPT_REQUEST,
  output [15:0] OUTPUT_PORT_VALUE,
  output OUTPUT_PORT_VALID,
  output INTERRUPT_PENDING,
  output INTERRUPT_ENABLED,
  output [11:0] RET_ADDR,
  output RET_ADDR_VALID,
  output IN_INTERRUPT_HANDLER
);

  wire interruptcontroller_1_p4, interruptcontroller_1_p5, interruptcontroller_1_p6,
       interruptcontroller_1_p7, interruptcontroller_1_p8, interruptcontroller_1_p9,
       interruptcontroller_1_p12, interruptcontroller_1_p14, outputmemorypath_1_p1, outputmemorypath_1_p2,
       outputmemorypath_1_p3, outputmemorypath_1_p4, outputmemorypath_1_p7, outputmemorypath_1_p8,
       outputmemorypath_1_p11;

  // OutputMemoryPath outputmemorypath_1: pin names not known; wires that end beside it: outputmemorypath_1_p1, outputmemorypath_1_p2, outputmemorypath_1_p3, outputmemorypath_1_p4, CLK, RESET, outputmemorypath_1_p7, outputmemorypath_1_p8, OUTPUT_PORT_VALUE, OUTPUT_PORT_VALID, outputmemorypath_1_p11
  // InterruptController interruptcontroller_1: pin names not known; wires that end beside it: RESET, CLK, INTERRUPT_REQUEST, interruptcontroller_1_p4, interruptcontroller_1_p5, interruptcontroller_1_p6, interruptcontroller_1_p7, interruptcontroller_1_p8, interruptcontroller_1_p9, INTERRUPT_PENDING, INTERRUPT_ENABLED, interruptcontroller_1_p12, RET_ADDR, interruptcontroller_1_p14, RET_ADDR_VALID, IN_INTERRUPT_HANDLER
  // CPUIntegrationBoundary cpuintegrationboundary_1: pin names not known; wires that end beside it: CLK, RESET, outputmemorypath_1_p7, outputmemorypath_1_p8, interruptcontroller_1_p9, interruptcontroller_1_p14, interruptcontroller_1_p12, outputmemorypath_1_p11, outputmemorypath_1_p1, outputmemorypath_1_p2, outputmemorypath_1_p4, outputmemorypath_1_p3, interruptcontroller_1_p4, interruptcontroller_1_p5, interruptcontroller_1_p6, interruptcontroller_1_p7, interruptcontroller_1_p8
endmodule

module CPUIntegrationBoundary (
  input  CLK,
  input  RESET,
  input  ILL_RET,
  input  RAM_READ_VALID,
  input  [11:0] TARGET_PC,
  input  [15:0] RAM_READ_VALUE,
  input  [11:0] CORE_ADDRESS,
  input  RAM_WRITE_ENABLE,
  output [15:0] READ_VALUE,
  output READ_VALID,
  output [11:0] ADDRESS,
  output [15:0] WRITE_VALUE,
  output WRITE_ENABLE,
  output WRITE_VALID,
  output INSTRUCTION_BOUNDARY,
  output ENABLE_REQUEST,
  output DISABLE_REQUEST,
  output RETURN_REQUEST,
  output [11:0] NEXT_PC
);

  TinyCPUMain tinycpumain_1 (
    .CLK(CLK), .RESET(RESET), .ILL_RET(ILL_RET), .INTERRUPT_ACCEPT(RAM_READ_VALID),
    .INTERRUPT_TARGET_PC(TARGET_PC), .EXTERNAL_MEMORY_VALUE(RAM_READ_VALUE),
    .PRINT_ADDRESS_VALUE(READ_VALUE), .PRINT_ADDRESS_VALID(READ_VALID), .EXTERNAL_WRITE_VALUE(WRITE_VALUE),
    .EXTERNAL_WRITE_VALID(WRITE_VALID), .EXTERNAL_WRITE_ENABLE(WRITE_ENABLE),
    .INSTRUCTION_BOUNDARY(INSTRUCTION_BOUNDARY), .ENABLE_INTERRUPTS_REQUEST(DISABLE_REQUEST),
    .DISABLE_INTERRUPTS_REQUEST(ENABLE_REQUEST), .RETURN_FROM_INTERRUPT_REQUEST(RETURN_REQUEST),
    .NEXT_PC(NEXT_PC));  // open: EXTERNAL_MEMORY_VALID, USE_EXTERNAL_MEMORY, PRINT_VALUE, ERROR_OVF, ERROR_DIV0, ERROR_ADDR, ERROR_INV, ERROR_ILL, ERROR_INPUT, PRINT_ENABLE, PRINT_ADDRESS_ENABLE, HALTED, HALTED_WITH_ERROR

  assign ADDRESS = CORE_ADDRESS;
endmodule

module OutputPort (
  input  [15:0] WRITE_VALUE,
  input  WRITE_VALID,
  input  WRITE_ENABLE,
  input  CLK,
  input  RESET,
  output [15:0] VALUE,
  output VALID
);

  wire OUTPUT_WRITE_ACCEPTED_out;

  and OUTPUT_WRITE_ACCEPTED (OUTPUT_WRITE_ACCEPTED_out, WRITE_VALID, WRITE_ENABLE);
  Register #(.width(16)) OUTPUT_VALUE (
    .D(WRITE_VALUE), .en(OUTPUT_WRITE_ACCEPTED_out), .clk(CLK), .Q(VALUE), .clr(RESET));
  Register #(.width(1)) OUTPUT_VALID (
    .D(WRITE_VALID), .en(OUTPUT_WRITE_ACCEPTED_out), .clk(CLK), .Q(VALID), .clr(RESET));
endmodule

module OutputMemoryPath (
  input  [15:0] RAM_READ_VALUE,
  input  RAM_READ_VALID,
  input  [11:0] ADDRESS,
  input  [15:0] WRITE_VALUE,
  input  WRITE_VALID,
  input  WRITE_ENABLE,
  input  CLK,
  input  RESET,
  output [15:0] READ_VALUE,
  output READ_VALID,
  output [15:0] OUTPUT_PORT_VALUE,
  output OUTPUT_PORT_VALID,
  output RAM_WRITE_ENABLE
);

  wire comparator_1_eq, OUTPUT_WRITE_GATE_out;

  Comparator #(.width(12)) comparator_1 (.a(ADDRESS), .b({12{1'b1}}), .eq(comparator_1_eq));  // open: gt, lt
  and OUTPUT_WRITE_GATE (OUTPUT_WRITE_GATE_out, WRITE_VALID, comparator_1_eq, WRITE_ENABLE);
  and RAM_WRITE_GATE (RAM_WRITE_ENABLE, ~comparator_1_eq, WRITE_ENABLE);  // AND_Gate
  Register #(.width(16)) OUTPUT_VALUE (
    .D(WRITE_VALUE), .en(OUTPUT_WRITE_GATE_out), .clk(CLK), .Q(OUTPUT_PORT_VALUE), .clr(RESET));
  Register #(.width(1)) OUTPUT_VALID (
    .D(WRITE_VALID), .en(OUTPUT_WRITE_GATE_out), .clk(CLK), .Q(OUTPUT_PORT_VALID), .clr(RESET));
  Multiplexer #(.width(16)) multiplexer_1 (
    .in0(RAM_READ_VALUE), .in1(OUTPUT_PORT_VALUE), .out(READ_VALUE), .sel(comparator_1_eq));
  Multiplexer multiplexer_2 (.in0(RAM_READ_VALID), .in1(OUTPUT_PORT_VALID), .out(READ_VALID), .sel(comparator_1_eq));

  // Notes on the sheet:
  //   OUTPUT MEMORY PATH — address 0xFFF selects output port
endmodule

module InterruptController (
  input  RESET,
  input  CLK,
  input  INTERRUPT_REQUEST,
  input  INSTRUCTION_BOUNDARY,
  input  ENABLE_REQUEST,
  input  DISABLE_REQUEST,
  input  RETURN_REQUEST,
  input  [11:0] NEXT_PC,
  output INTERRUPT_ACCEPT,
  output INTERRUPT_PENDING,
  output INTERRUPT_ENABLED,
  output ILL_RET,
  output [11:0] RET_ADDR,
  output [11:0] TARGET_PC,
  output RET_ADDR_VALID,
  output IN_INTERRUPT_HANDLER
);

  wire HANDLER_HOLD_out, HANDLER_NEXT_out, MASK_HOLD_out, MASK_NEXT_out, PENDING_HOLD_UNTIL_ACCEPT_out,
       PENDING_SET_OR_HOLD_out, REQUEST_LEVEL_q, RETURN_VALID_HOLD_out, RETURN_VALID_NEXT_out,
       RISING_EDGE_DETECT_out, VALID_RETURN_GATE_out;

  and RISING_EDGE_DETECT (RISING_EDGE_DETECT_out, ~REQUEST_LEVEL_q, INTERRUPT_REQUEST);  // AND_Gate
  and PENDING_HOLD_UNTIL_ACCEPT (PENDING_HOLD_UNTIL_ACCEPT_out, INTERRUPT_PENDING, ~INTERRUPT_ACCEPT);  // AND_Gate
  and MASK_HOLD (MASK_HOLD_out, INTERRUPT_ENABLED, ~DISABLE_REQUEST, ~INTERRUPT_ACCEPT);  // AND_Gate
  and RETURN_VALID_HOLD (RETURN_VALID_HOLD_out, RET_ADDR_VALID, ~VALID_RETURN_GATE_out);  // AND_Gate
  and HANDLER_HOLD (HANDLER_HOLD_out, IN_INTERRUPT_HANDLER, ~VALID_RETURN_GATE_out);  // AND_Gate
  or PENDING_SET_OR_HOLD (PENDING_SET_OR_HOLD_out, RISING_EDGE_DETECT_out, PENDING_HOLD_UNTIL_ACCEPT_out);
  or MASK_NEXT (MASK_NEXT_out, ENABLE_REQUEST, VALID_RETURN_GATE_out, MASK_HOLD_out);
  or RETURN_VALID_NEXT (RETURN_VALID_NEXT_out, INTERRUPT_ACCEPT, RETURN_VALID_HOLD_out);
  or HANDLER_NEXT (HANDLER_NEXT_out, INTERRUPT_ACCEPT, HANDLER_HOLD_out);
  Register #(.width(1)) REQUEST_LEVEL (.D(INTERRUPT_REQUEST), .en(1'b1), .clk(CLK), .Q(REQUEST_LEVEL_q), .clr(RESET));
  Register #(.width(1)) register_1 (
    .D(PENDING_SET_OR_HOLD_out), .en(1'b1), .clk(CLK), .Q(INTERRUPT_PENDING), .clr(RESET));
  Register #(.width(1)) register_2 (.D(MASK_NEXT_out), .en(1'b1), .clk(CLK), .Q(INTERRUPT_ENABLED), .clr(RESET));
  Register #(.width(12)) register_3 (.D(NEXT_PC), .en(INTERRUPT_ACCEPT), .clk(CLK), .Q(RET_ADDR), .clr(RESET));
  Register #(.width(1)) register_4 (.D(RETURN_VALID_NEXT_out), .en(1'b1), .clk(CLK), .Q(RET_ADDR_VALID), .clr(RESET));
  Register #(.width(1)) register_5 (.D(HANDLER_NEXT_out), .en(1'b1), .clk(CLK), .Q(IN_INTERRUPT_HANDLER), .clr(RESET));
  and INTERRUPT_ACCEPT_GATE (INTERRUPT_ACCEPT, INSTRUCTION_BOUNDARY, INTERRUPT_PENDING, INTERRUPT_ENABLED, ~IN_INTERRUPT_HANDLER);  // AND_Gate
  and VALID_RETURN_GATE (VALID_RETURN_GATE_out, RETURN_REQUEST, RET_ADDR_VALID, IN_INTERRUPT_HANDLER);
  and ILL_RET_GATE (ILL_RET, RETURN_REQUEST, ~VALID_RETURN_GATE_out);  // AND_Gate
  Multiplexer #(.width(12)) multiplexer_1 (.in0(12'hff0), .in1(RET_ADDR), .out(TARGET_PC), .sel(VALID_RETURN_GATE_out));

  // Notes on the sheet:
  //   EDGE / INPUTS
  //   NEXT-STATE LOGIC
  //   feedback buses: ACCEPT / VALID_RETURN
  //   STATE REGISTERS
  //   ACCEPT / RETURN DECODE
endmodule
